# Fritzing sketch circuit-diagram (saved by Fritzing 0.9.5d)
circuit board: 8.46667cm x 5.64444cm
breadboards: 1

parts:
  U1 = NodeMCU V1.0
  LCD = LCD1602-I2C
  R1 = PHOTOCELL [package=photocell-kit]
  R3 = Resistor [tolerance=±5% resistance=10k package="2512 [SMD]"]
  R4 = Resistor [tolerance=±5% resistance=10k package="2512 [SMD]"]
  Componente1 = Soil Moisture Sensor
  S1 = Momentary Switch [package=ksa_sealed_tac_switch]
  DHT2 = DHT11 Humitidy and Temperature Sensor
  LED1 = LEDs [package=led10mm]
  R5 = Resistor [tolerance=±5% resistance=220 package="2512 [SMD]"]
  R7 = Resistor [tolerance=±5% resistance=220 package="2512 [SMD]"]
  LED2 = LEDs [package=led10mm]

nets:
  N1: U1.D0, LED2.A
  N2: U1.D1, LCD.SCL
  N3: U1.D2, LCD.SDA
  N4: U1.D3, R3.Pin_0, DHT2.DATA
  N5: U1.D4, LED1.A
  3V3: U1.3V3, R3.Pin_1, DHT2.VDD, R5.Pin_1, R7.Pin_1
  GND: U1.GND, LCD.GND, S1.3, DHT2.GND
  N6: U1.D5, R4.Pin_0
  N7: U1.D6, R1.P$1
  N8: U1.D7, Componente1.GND
  N9: U1.D8, Componente1.VCC
  VIN: U1.Vin, LCD.VCC
  N10: U1.SD3, S1.4
  N11: U1.A0, R1.P$2, R4.Pin_1, Componente1.SIG
  N12: LED1.C, R5.Pin_0
  N13: R7.Pin_0, LED2.C

custom parts:
  NodeMCU V1.0: ESP8266 based NodeMCU
  LCD1602-I2C: A standard character display, usually with 2x16 characters. Comes in many colors with LCM1602 IIC attached.
  DHT11 Humitidy and Temperature Sensor: DHT11 Humidity and Temperature Sensor
